// Logisim project ergasia 2.circ as structural Verilog: 2 circuits, main circuit main
module main (
  input  Preset,
  input  J,
  input  Clock,
  input  K,
  input  Clear,
  output Q,
  output Q_prime
);

  wire nand_1_out, nand_2_out, nand_3_out, nand_4_out, nand_5_out, nand_6_out, not_1_out;

  not not_1 (not_1_out, Clock);
  nand nand_1 (nand_1_out, Q_prime, J, not_1_out);
  nand nand_2 (nand_2_out, not_1_out, K, Q);
  nand nand_3 (nand_3_out, Preset, nand_1_out, nand_4_out);
  nand nand_4 (nand_4_out, nand_3_out, nand_2_out, Clear);
  nand nand_5 (nand_5_out, nand_3_out, Clock);
  nand nand_6 (nand_6_out, Clock, nand_4_out);
  nand nand_7 (Q, Preset, nand_5_out, Q_prime);
  nand nand_8 (Q_prime, Q, nand_6_out, Clear);
endmodule

module _5_BIT_RING_COUNTER (
  input  P0,
  input  P1,
  input  P2,
  input  P3,
  input  P4,
  input  Clear,
  output out_7,
  output out_8,
  output out_9,
  output out_10,
  output out_11
);

  wire Clock_out, main_1_q_prime, main_2_q_prime, main_3_q_prime, main_4_q_prime, main_5_q_prime, not_1_out,
       not_2_out, not_3_out, not_4_out, not_5_out, not_6_out;

  Clock Clock (.out(Clock_out));
  not not_1 (not_1_out, P0);
  not not_2 (not_2_out, Clear);
  main main_1 (
    .Preset(not_1_out), .J(out_11), .Clock(Clock_out), .K(main_5_q_prime), .Clear(not_2_out), .Q(out_7),
    .Q_prime(main_1_q_prime));
  not not_3 (not_3_out, P1);
  main main_2 (
    .Preset(not_3_out), .J(out_7), .Clock(Clock_out), .K(main_1_q_prime), .Clear(not_2_out), .Q(out_8),
    .Q_prime(main_2_q_prime));
  not not_4 (not_4_out, P2);
  main main_3 (
    .Preset(not_4_out), .J(out_8), .Clock(Clock_out), .K(main_2_q_prime), .Clear(not_2_out), .Q(out_9),
    .Q_prime(main_3_q_prime));
  not not_5 (not_5_out, P3);
  main main_4 (
    .Preset(not_5_out), .J(out_9), .Clock(Clock_out), .K(main_3_q_prime), .Clear(not_2_out), .Q(out_10),
    .Q_prime(main_4_q_prime));
  not not_6 (not_6_out, P4);
  main main_5 (
    .Preset(not_6_out), .J(out_10), .Clock(Clock_out), .K(main_4_q_prime), .Clear(not_2_out), .Q(out_11),
    .Q_prime(main_5_q_prime));

  // Notes on the sheet:
  //   Για να να γινουν οι αρχικες τιμες 0, θέτουμε το Clear σε 1 και μετά το ξανακάνουμε 0.
  //   Οταν ολα τα Preset και το Clear ειναι 0 και εχουμε θέσει το επιθυμητό Preset, το counter ειναι ετοιμο για χρήση.
  //   Για να χρησιμοποιήσουμε το Preset, θέτουμε στο επιθημιτο input την τιμη 1 και μετά ξανα την τιμη 0.
endmodule
