// Logisim project ergasia1_.circ as structural Verilog: 1 circuit, main circuit main
module main (
  input  [1:0] A,
  input  [1:0] B,
  input  [2:0] SELECTION_BITS,
  output [1:0] OUTPUT,
  output Cout
);

  wire adder_1_cout, adder_2_cout, and_3_out, and_4_out, not_5_out;
  wire [1:0] adder_1_out, adder_2_out, and_1_out, not_1_out, not_3_out, or_1_out;

  not not_1 (not_1_out[0], A[0]);
  not not_2 (not_1_out[1], A[1]);
  and and_1 (and_1_out[0], A[0], B[0]);
  not not_3 (not_3_out[0], B[0]);
  not not_4 (not_3_out[1], B[1]);
  and and_2 (and_1_out[1], B[1], A[1]);
  or or_1 (or_1_out[0], B[0], A[0]);
  or or_2 (or_1_out[1], A[1], B[1]);
  Adder #(.width(2)) adder_1 (.a(A), .b(2'b01), .out(adder_1_out), .cout(adder_1_cout));  // open: cin
  Adder #(.width(2)) adder_2 (.a(B), .b(2'b01), .out(adder_2_out), .cout(adder_2_cout));  // open: cin
  not not_5 (not_5_out, SELECTION_BITS[0]);
  and and_3 (and_3_out, adder_1_cout, not_5_out);
  Multiplexer #(.select(3), .width(2)) multiplexer_1 (
    .in0(not_1_out), .in1(not_3_out), .in2(and_1_out), .in3(or_1_out), .in4(adder_1_out), .in5(adder_2_out),
    .out(OUTPUT), .sel(SELECTION_BITS));  // open: in6, in7, en
  and and_4 (and_4_out, SELECTION_BITS[0], adder_2_cout);
  or or_3 (Cout, and_3_out, and_4_out);
endmodule
